// Logisim project Aula1.circ as structural Verilog: 6 circuits, main circuit main
module main (
  input  in_1,
  input  in_2,
  input  in_3,
  input  in_4,
  input  SAVE,
  input  reset,
  output out_7,
  output out_8,
  output out_9,
  output out_10
);

  D_Flip_Flop d_ff_1 (.clk(in_2), .D(in_1), .Q(out_7), .reset(reset));  // open: Qn, preset, en
  D_Flip_Flop d_ff_2 (.clk(in_2), .D(in_2), .Q(out_8), .reset(reset));  // open: Qn, preset, en
  D_Flip_Flop d_ff_3 (.clk(in_2), .D(in_2), .Q(out_9), .reset(reset));  // open: Qn, preset, en
  D_Flip_Flop d_ff_4 (.clk(in_2), .D(in_3), .Q(out_10), .reset(reset));  // open: Qn, preset, en

  assign in_4 = in_2;
  assign SAVE = in_2;
endmodule

module BancoReg4bit (
  input  [3:0] INPUT,
  input  SAVE,
  input  Reset,
  output [3:0] OUT
);

  D_Flip_Flop d_ff_1 (.clk(SAVE), .D(INPUT[3]), .Q(OUT[3]), .reset(Reset));  // open: Qn, preset, en
  D_Flip_Flop d_ff_2 (.clk(SAVE), .D(INPUT[2]), .Q(OUT[2]), .reset(Reset));  // open: Qn, preset, en
  D_Flip_Flop d_ff_3 (.clk(SAVE), .D(INPUT[1]), .Q(OUT[1]), .reset(Reset));  // open: Qn, preset, en
  D_Flip_Flop d_ff_4 (.clk(SAVE), .D(INPUT[0]), .Q(OUT[0]), .reset(Reset));  // open: Qn, preset, en
endmodule

module BancoReg8bit (
  input  [3:0] in_1,
  input  in_2,
  input  in_3,
  input  in_4,
  input  in_5,
  input  in_6,
  input  in_7,
  input  in_8,
  input  in_9,
  input  in_10,
  output [3:0] out_11,
  output [3:0] out_12,
  output [3:0] out_13,
  output [3:0] out_14,
  output [3:0] out_15,
  output [3:0] out_16,
  output [3:0] out_17,
  output [3:0] out_18
);

  BancoReg4bit bancoreg4bit_1 (.SAVE(in_2), .Reset(in_3), .OUT(out_11), .INPUT(in_1));
  BancoReg4bit bancoreg4bit_2 (.SAVE(in_4), .Reset(in_3), .OUT(out_12), .INPUT(in_1));
  BancoReg4bit bancoreg4bit_3 (.SAVE(in_5), .Reset(in_3), .OUT(out_13), .INPUT(in_1));
  BancoReg4bit bancoreg4bit_4 (.SAVE(in_6), .Reset(in_3), .OUT(out_14), .INPUT(in_1));
  BancoReg4bit bancoreg4bit_5 (.SAVE(in_7), .Reset(in_3), .OUT(out_15), .INPUT(in_1));
  BancoReg4bit bancoreg4bit_6 (.SAVE(in_8), .Reset(in_3), .OUT(out_16), .INPUT(in_1));
  BancoReg4bit bancoreg4bit_7 (.SAVE(in_9), .Reset(in_3), .OUT(out_17), .INPUT(in_1));
  BancoReg4bit bancoreg4bit_8 (.SAVE(in_10), .Reset(in_3), .OUT(out_18), .INPUT(in_1));
endmodule

module BancoReg8bit_completo (
  input  [3:0] Data,
  input  Reset,
  input  CLK,
  input  [2:0] WReg,
  output [3:0] ViewRegA,
  output [2:0] RegA,
  output [3:0] ViewRegB,
  output [2:0] RegB
);

  wire demultiplexer_1_out0, demultiplexer_1_out1, demultiplexer_1_out2, demultiplexer_1_out3,
       demultiplexer_1_out4, demultiplexer_1_out5, demultiplexer_1_out6, demultiplexer_1_out7;
  wire [3:0] bancoreg4bit_1_out, bancoreg4bit_2_out, bancoreg4bit_3_out, bancoreg4bit_4_out,
       bancoreg4bit_5_out, bancoreg4bit_6_out, bancoreg4bit_7_out, bancoreg4bit_8_out;

  Demultiplexer #(.select(3)) demultiplexer_1 (
    .out0(demultiplexer_1_out0), .out1(demultiplexer_1_out1), .out2(demultiplexer_1_out2),
    .out3(demultiplexer_1_out3), .out4(demultiplexer_1_out4), .out5(demultiplexer_1_out5),
    .out6(demultiplexer_1_out6), .out7(demultiplexer_1_out7), .in(CLK), .sel(WReg));  // open: en
  BancoReg4bit bancoreg4bit_1 (.SAVE(demultiplexer_1_out0), .Reset(Reset), .OUT(bancoreg4bit_1_out), .INPUT(Data));
  BancoReg4bit bancoreg4bit_2 (.SAVE(demultiplexer_1_out1), .Reset(Reset), .OUT(bancoreg4bit_2_out), .INPUT(Data));
  BancoReg4bit bancoreg4bit_3 (.SAVE(demultiplexer_1_out2), .Reset(Reset), .OUT(bancoreg4bit_3_out), .INPUT(Data));
  BancoReg4bit bancoreg4bit_4 (.SAVE(demultiplexer_1_out3), .Reset(Reset), .OUT(bancoreg4bit_4_out), .INPUT(Data));
  BancoReg4bit bancoreg4bit_5 (.SAVE(demultiplexer_1_out4), .Reset(Reset), .OUT(bancoreg4bit_5_out), .INPUT(Data));
  BancoReg4bit bancoreg4bit_6 (.SAVE(demultiplexer_1_out5), .Reset(Reset), .OUT(bancoreg4bit_6_out), .INPUT(Data));
  BancoReg4bit bancoreg4bit_7 (.SAVE(demultiplexer_1_out6), .Reset(Reset), .OUT(bancoreg4bit_7_out), .INPUT(Data));
  BancoReg4bit bancoreg4bit_8 (.SAVE(demultiplexer_1_out7), .Reset(Reset), .OUT(bancoreg4bit_8_out), .INPUT(Data));
  Multiplexer #(.select(3), .width(4)) multiplexer_1 (
    .in0(bancoreg4bit_1_out), .in1(bancoreg4bit_2_out), .in2(bancoreg4bit_3_out), .in3(bancoreg4bit_4_out),
    .in4(bancoreg4bit_5_out), .in5(bancoreg4bit_6_out), .in6(bancoreg4bit_7_out), .in7(bancoreg4bit_8_out),
    .out(ViewRegA), .sel(RegA));  // open: en
  Multiplexer #(.select(3), .width(4)) multiplexer_2 (
    .in0(bancoreg4bit_1_out), .in1(bancoreg4bit_2_out), .in2(bancoreg4bit_3_out), .in3(bancoreg4bit_4_out),
    .in4(bancoreg4bit_5_out), .in5(bancoreg4bit_6_out), .in6(bancoreg4bit_7_out), .in7(bancoreg4bit_8_out),
    .out(ViewRegB), .sel(RegB));  // open: en
endmodule

module BancoReg32bit (
  input  [3:0] in_1,
  input  in_2,
  input  in_3,
  input  in_4,
  input  in_5,
  input  in_6,
  input  in_7,
  input  in_8,
  input  in_9,
  input  in_10,
  input  in_11,
  input  in_12,
  input  in_13,
  input  in_14,
  input  in_15,
  input  in_16,
  input  in_17,
  input  in_18,
  input  in_19,
  input  in_20,
  input  in_21,
  input  in_22,
  input  in_23,
  input  in_24,
  input  in_25,
  input  in_26,
  input  in_27,
  input  in_28,
  input  in_29,
  input  in_30,
  input  in_31,
  input  in_32,
  input  in_33,
  input  in_34,
  output [3:0] out_35,
  output [3:0] out_36,
  output [3:0] out_37,
  output [3:0] out_38,
  output [3:0] out_39,
  output [3:0] out_40,
  output [3:0] out_41,
  output [3:0] out_42,
  output [3:0] out_43,
  output [3:0] out_44,
  output [3:0] out_45,
  output [3:0] out_46,
  output [3:0] out_47,
  output [3:0] out_48,
  output [3:0] out_49,
  output [3:0] out_50,
  output [3:0] out_51,
  output [3:0] out_52,
  output [3:0] out_53,
  output [3:0] out_54,
  output [3:0] out_55,
  output [3:0] out_56,
  output [3:0] out_57,
  output [3:0] out_58,
  output [3:0] out_59,
  output [3:0] out_60,
  output [3:0] out_61,
  output [3:0] out_62,
  output [3:0] out_63,
  output [3:0] out_64,
  output [3:0] out_65,
  output [3:0] out_66
);

  BancoReg4bit bancoreg4bit_1 (.SAVE(in_2), .Reset(in_3), .OUT(out_35), .INPUT(in_1));
  BancoReg4bit bancoreg4bit_2 (.SAVE(in_4), .Reset(in_3), .OUT(out_36), .INPUT(in_1));
  BancoReg4bit bancoreg4bit_3 (.SAVE(in_5), .Reset(in_3), .OUT(out_37), .INPUT(in_1));
  BancoReg4bit bancoreg4bit_4 (.SAVE(in_6), .Reset(in_3), .OUT(out_38), .INPUT(in_1));
  BancoReg4bit bancoreg4bit_5 (.SAVE(in_7), .Reset(in_3), .OUT(out_39), .INPUT(in_1));
  BancoReg4bit bancoreg4bit_6 (.SAVE(in_8), .Reset(in_3), .OUT(out_40), .INPUT(in_1));
  BancoReg4bit bancoreg4bit_7 (.SAVE(in_9), .Reset(in_3), .OUT(out_41), .INPUT(in_1));
  BancoReg4bit bancoreg4bit_8 (.SAVE(in_10), .Reset(in_3), .OUT(out_42), .INPUT(in_1));
  BancoReg4bit bancoreg4bit_9 (.SAVE(in_11), .Reset(in_3), .OUT(out_43), .INPUT(in_1));
  BancoReg4bit bancoreg4bit_10 (.SAVE(in_12), .Reset(in_3), .OUT(out_44), .INPUT(in_1));
  BancoReg4bit bancoreg4bit_11 (.SAVE(in_13), .Reset(in_3), .OUT(out_45), .INPUT(in_1));
  BancoReg4bit bancoreg4bit_12 (.SAVE(in_14), .Reset(in_3), .OUT(out_46), .INPUT(in_1));
  BancoReg4bit bancoreg4bit_13 (.SAVE(in_15), .Reset(in_3), .OUT(out_47), .INPUT(in_1));
  BancoReg4bit bancoreg4bit_14 (.SAVE(in_16), .Reset(in_3), .OUT(out_48), .INPUT(in_1));
  BancoReg4bit bancoreg4bit_15 (.SAVE(in_17), .Reset(in_3), .OUT(out_49), .INPUT(in_1));
  BancoReg4bit bancoreg4bit_16 (.SAVE(in_18), .Reset(in_3), .OUT(out_50), .INPUT(in_1));
  BancoReg4bit bancoreg4bit_17 (.SAVE(in_19), .Reset(in_3), .OUT(out_51), .INPUT(in_1));
  BancoReg4bit bancoreg4bit_18 (.SAVE(in_20), .Reset(in_3), .OUT(out_52), .INPUT(in_1));
  BancoReg4bit bancoreg4bit_19 (.SAVE(in_21), .Reset(in_3), .OUT(out_53), .INPUT(in_1));
  BancoReg4bit bancoreg4bit_20 (.SAVE(in_22), .Reset(in_3), .OUT(out_54), .INPUT(in_1));
  BancoReg4bit bancoreg4bit_21 (.SAVE(in_23), .Reset(in_3), .OUT(out_55), .INPUT(in_1));
  BancoReg4bit bancoreg4bit_22 (.SAVE(in_24), .Reset(in_3), .OUT(out_56), .INPUT(in_1));
  BancoReg4bit bancoreg4bit_23 (.SAVE(in_25), .Reset(in_3), .OUT(out_57), .INPUT(in_1));
  BancoReg4bit bancoreg4bit_24 (.SAVE(in_26), .Reset(in_3), .OUT(out_58), .INPUT(in_1));
  BancoReg4bit bancoreg4bit_25 (.SAVE(in_27), .Reset(in_3), .OUT(out_59), .INPUT(in_1));
  BancoReg4bit bancoreg4bit_26 (.SAVE(in_28), .Reset(in_3), .OUT(out_60), .INPUT(in_1));
  BancoReg4bit bancoreg4bit_27 (.SAVE(in_29), .Reset(in_3), .OUT(out_61), .INPUT(in_1));
  BancoReg4bit bancoreg4bit_28 (.SAVE(in_30), .Reset(in_3), .OUT(out_62), .INPUT(in_1));
  BancoReg4bit bancoreg4bit_29 (.SAVE(in_31), .Reset(in_3), .OUT(out_63), .INPUT(in_1));
  BancoReg4bit bancoreg4bit_30 (.SAVE(in_32), .Reset(in_3), .OUT(out_64), .INPUT(in_1));
  BancoReg4bit bancoreg4bit_31 (.SAVE(in_33), .Reset(in_3), .OUT(out_65), .INPUT(in_1));
  BancoReg4bit bancoreg4bit_32 (.SAVE(in_34), .Reset(in_3), .OUT(out_66), .INPUT(in_1));
endmodule

module rascunho (
  input  [3:0] in_1,
  input  in_2,
  input  in_3,
  input  in_4,
  input  in_5,
  input  in_6,
  input  in_7,
  input  in_8,
  input  in_9,
  input  in_10,
  input  in_11,
  input  in_12,
  input  in_13,
  input  in_14,
  input  in_15,
  input  in_16,
  input  in_17,
  input  in_18,
  input  in_19,
  input  in_20,
  input  in_21,
  input  in_22,
  input  in_23,
  input  in_24,
  input  in_25,
  input  in_26,
  input  in_27,
  input  in_28,
  input  in_29,
  input  in_30,
  input  in_31,
  input  in_32,
  input  in_33,
  input  in_34,
  output [3:0] out_35,
  output [3:0] out_36,
  output [3:0] out_37,
  output [3:0] out_38,
  output [3:0] out_39,
  output [3:0] out_40,
  output [3:0] out_41,
  output [3:0] out_42,
  output [3:0] out_43,
  output [3:0] out_44,
  output [3:0] out_45,
  output [3:0] out_46,
  output [3:0] out_47,
  output [3:0] out_48,
  output [3:0] out_49,
  output [3:0] out_50,
  output [3:0] out_51,
  output [3:0] out_52,
  output [3:0] out_53,
  output [3:0] out_54,
  output [3:0] out_55,
  output [3:0] out_56,
  output [3:0] out_57,
  output [3:0] out_58,
  output [3:0] out_59,
  output [3:0] out_60,
  output [3:0] out_61,
  output [3:0] out_62,
  output [3:0] out_63,
  output [3:0] out_64,
  output [3:0] out_65,
  output [3:0] out_66
);

  BancoReg4bit bancoreg4bit_1 (.SAVE(in_2), .Reset(in_3), .OUT(out_35), .INPUT(in_1));
  BancoReg4bit bancoreg4bit_2 (.SAVE(in_4), .Reset(in_3), .OUT(out_36), .INPUT(in_1));
  BancoReg4bit bancoreg4bit_3 (.SAVE(in_5), .Reset(in_3), .OUT(out_37), .INPUT(in_1));
  BancoReg4bit bancoreg4bit_4 (.SAVE(in_6), .Reset(in_3), .OUT(out_38), .INPUT(in_1));
  BancoReg4bit bancoreg4bit_5 (.SAVE(in_7), .Reset(in_3), .OUT(out_39), .INPUT(in_1));
  BancoReg4bit bancoreg4bit_6 (.SAVE(in_8), .Reset(in_3), .OUT(out_40), .INPUT(in_1));
  BancoReg4bit bancoreg4bit_7 (.SAVE(in_9), .Reset(in_3), .OUT(out_41), .INPUT(in_1));
  BancoReg4bit bancoreg4bit_8 (.SAVE(in_10), .Reset(in_3), .OUT(out_42), .INPUT(in_1));
  BancoReg4bit bancoreg4bit_9 (.SAVE(in_11), .Reset(in_3), .OUT(out_43), .INPUT(in_1));
  BancoReg4bit bancoreg4bit_10 (.SAVE(in_12), .Reset(in_3), .OUT(out_44), .INPUT(in_1));
  BancoReg4bit bancoreg4bit_11 (.SAVE(in_13), .Reset(in_3), .OUT(out_45), .INPUT(in_1));
  BancoReg4bit bancoreg4bit_12 (.SAVE(in_14), .Reset(in_3), .OUT(out_46), .INPUT(in_1));
  BancoReg4bit bancoreg4bit_13 (.SAVE(in_15), .Reset(in_3), .OUT(out_47), .INPUT(in_1));
  BancoReg4bit bancoreg4bit_14 (.SAVE(in_16), .Reset(in_3), .OUT(out_48), .INPUT(in_1));
  BancoReg4bit bancoreg4bit_15 (.SAVE(in_17), .Reset(in_3), .OUT(out_49), .INPUT(in_1));
  BancoReg4bit bancoreg4bit_16 (.SAVE(in_18), .Reset(in_3), .OUT(out_50), .INPUT(in_1));
  BancoReg4bit bancoreg4bit_17 (.SAVE(in_19), .Reset(in_3), .OUT(out_51), .INPUT(in_1));
  BancoReg4bit bancoreg4bit_18 (.SAVE(in_20), .Reset(in_3), .OUT(out_52), .INPUT(in_1));
  BancoReg4bit bancoreg4bit_19 (.SAVE(in_21), .Reset(in_3), .OUT(out_53), .INPUT(in_1));
  BancoReg4bit bancoreg4bit_20 (.SAVE(in_22), .Reset(in_3), .OUT(out_54), .INPUT(in_1));
  BancoReg4bit bancoreg4bit_21 (.SAVE(in_23), .Reset(in_3), .OUT(out_55), .INPUT(in_1));
  BancoReg4bit bancoreg4bit_22 (.SAVE(in_24), .Reset(in_3), .OUT(out_56), .INPUT(in_1));
  BancoReg4bit bancoreg4bit_23 (.SAVE(in_25), .Reset(in_3), .OUT(out_57), .INPUT(in_1));
  BancoReg4bit bancoreg4bit_24 (.SAVE(in_26), .Reset(in_3), .OUT(out_58), .INPUT(in_1));
  BancoReg4bit bancoreg4bit_25 (.SAVE(in_27), .Reset(in_3), .OUT(out_59), .INPUT(in_1));
  BancoReg4bit bancoreg4bit_26 (.SAVE(in_28), .Reset(in_3), .OUT(out_60), .INPUT(in_1));
  BancoReg4bit bancoreg4bit_27 (.SAVE(in_29), .Reset(in_3), .OUT(out_61), .INPUT(in_1));
  BancoReg4bit bancoreg4bit_28 (.SAVE(in_30), .Reset(in_3), .OUT(out_62), .INPUT(in_1));
  BancoReg4bit bancoreg4bit_29 (.SAVE(in_31), .Reset(in_3), .OUT(out_63), .INPUT(in_1));
  BancoReg4bit bancoreg4bit_30 (.SAVE(in_32), .Reset(in_3), .OUT(out_64), .INPUT(in_1));
  BancoReg4bit bancoreg4bit_31 (.SAVE(in_33), .Reset(in_3), .OUT(out_65), .INPUT(in_1));
  BancoReg4bit bancoreg4bit_32 (.SAVE(in_34), .Reset(in_3), .OUT(out_66), .INPUT(in_1));
endmodule
