// Logisim project SD.circ as structural Verilog: 4 circuits, main circuit Mux2
module Mux2 (
  input  A,
  input  B,
  input  Sel,
  output out_4
);

  wire and_1_out, and_2_out;

  and and_1 (and_1_out, A, ~Sel);  // AND_Gate
  and and_2 (and_2_out, B, Sel);
  or or_1 (out_4, and_1_out, and_2_out);
endmodule

module Mux4 (
  input  A,
  input  B,
  input  C,
  input  D,
  input  SEL_0,
  input  SEL_1,
  output out_7
);

  wire mux2_1_out_4, mux2_2_out_4;

  Mux2 mux2_1 (.A(C), .B(D), .Sel(SEL_1), .out_4(mux2_1_out_4));
  Mux2 mux2_2 (.A(A), .B(B), .Sel(SEL_1), .out_4(mux2_2_out_4));
  Mux2 mux2_3 (.A(mux2_2_out_4), .B(mux2_1_out_4), .Sel(SEL_0), .out_4(out_7));
endmodule

module Mux8 (
  input  A,
  input  B,
  input  C,
  input  D,
  input  E,
  input  F,
  input  G,
  input  H,
  input  SEL_0,
  input  SEL_1,
  input  SEL_2,
  output out_12
);

  wire mux4_1_out_7, mux4_2_out_7;

  Mux4 mux4_1 (.A(E), .B(F), .C(G), .D(H), .SEL_0(SEL_1), .SEL_1(SEL_2), .out_7(mux4_1_out_7));
  Mux4 mux4_2 (.A(A), .B(B), .C(C), .D(D), .SEL_0(SEL_1), .SEL_1(SEL_2), .out_7(mux4_2_out_7));
  Mux2 mux2_1 (.A(mux4_2_out_7), .B(mux4_1_out_7), .Sel(SEL_0), .out_4(out_12));
endmodule

module Mux16 (
  input  A,
  input  B,
  input  C,
  input  D,
  input  E,
  input  F,
  input  G,
  input  H,
  input  I,
  input  J,
  input  K,
  input  L,
  input  M,
  input  N,
  input  O,
  input  P,
  input  S0,
  input  S1,
  input  S2,
  input  S3,
  output out_21
);

  wire mux8_1_out_12, mux8_2_out_12;

  Mux8 mux8_1 (
    .A(I), .B(J), .C(K), .D(L), .E(M), .F(N), .G(O), .H(P), .SEL_0(S1), .SEL_1(S2), .SEL_2(S3),
    .out_12(mux8_1_out_12));
  Mux8 mux8_2 (
    .A(A), .B(B), .C(C), .D(D), .E(E), .F(F), .G(G), .H(H), .SEL_0(S1), .SEL_1(S2), .SEL_2(S3),
    .out_12(mux8_2_out_12));
  Mux2 mux2_1 (.A(mux8_2_out_12), .B(mux8_1_out_12), .Sel(S0), .out_4(out_21));
endmodule
