// Logisim project tentativa.circ as structural Verilog
module mux2 (
  input  A,
  input  B,
  input  Sel,
  output S
);

  wire and_1_out, and_2_out;

  and and_1 (and_1_out, A, ~Sel);  // AND_Gate
  and and_2 (and_2_out, B, Sel);
  LED led_1 (.in(and_1_out));
  or or_1 (S, and_1_out, and_2_out);
  LED led_2 (.in(and_2_out));
endmodule

module mux2b (
  input  [31:0] A,
  input  [31:0] B,
  input  Sel,
  output [31:0] S
);

  wire [31:0] and_1_out, and_2_out;

  assign and_1_out = A & ~{32{Sel}};  // AND_Gate and_1, 32 bits wide
  assign and_2_out = B & {32{Sel}};  // AND_Gate and_2, 32 bits wide
  assign S = and_1_out | and_2_out;  // OR_Gate or_1, 32 bits wide
endmodule

module mux4 (
  input  A,
  input  B,
  input  C,
  input  D,
  input  Sel1,
  input  Sel0,
  output out_7
);

  wire mux2_1_s, mux2_2_s;

  mux2 mux2_1 (.A(A), .B(B), .Sel(Sel0), .S(mux2_1_s));
  mux2 mux2_2 (.A(C), .B(D), .Sel(Sel0), .S(mux2_2_s));
  mux2 mux2_3 (.A(mux2_1_s), .B(mux2_2_s), .Sel(Sel1), .S(out_7));
endmodule

module mux4b (
  input  A,
  input  B,
  input  C,
  input  D,
  input  [1:0] in_5,
  output out_6
);

  wire mux2_1_s, mux2_2_s;

  mux2 mux2_1 (.A(A), .B(B), .Sel(in_5[0]), .S(mux2_1_s));
  mux2 mux2_2 (.A(C), .B(D), .Sel(in_5[0]), .S(mux2_2_s));
  mux2 mux2_3 (.A(mux2_1_s), .B(mux2_2_s), .Sel(in_5[1]), .S(out_6));
endmodule

module mux8 (
  input  l0,
  input  l1,
  input  l2,
  input  l3,
  input  l4,
  input  l5,
  input  l6,
  input  l7,
  input  in_9,
  input  in_10,
  input  in_11,
  output out_12
);

  wire mux4_1_out_7, mux4_2_out_7;

  mux4 mux4_1 (.A(l0), .B(l1), .C(l2), .D(l3), .Sel1(in_10), .Sel0(in_11), .out_7(mux4_1_out_7));
  mux4 mux4_2 (.A(l4), .B(l5), .C(l6), .D(l7), .Sel1(in_10), .Sel0(in_11), .out_7(mux4_2_out_7));
  mux2 mux2_1 (.A(mux4_1_out_7), .B(mux4_2_out_7), .Sel(in_9), .S(out_12));
endmodule

module mux8b (
  input  l0,
  input  l1,
  input  l2,
  input  l3,
  input  l4,
  input  l5,
  input  l6,
  input  l7,
  input  [2:0] in_9,
  output out_10
);

  wire mux4_1_out_7, mux4_2_out_7;

  mux4 mux4_1 (.A(l0), .B(l1), .C(l2), .D(l3), .Sel1(in_9[1]), .Sel0(in_9[0]), .out_7(mux4_1_out_7));
  mux4 mux4_2 (.A(l4), .B(l5), .C(l6), .D(l7), .Sel1(in_9[1]), .Sel0(in_9[0]), .out_7(mux4_2_out_7));
  mux2 mux2_1 (.A(mux4_1_out_7), .B(mux4_2_out_7), .Sel(in_9[2]), .S(out_10));
endmodule

module mux16 (
  input  l0,
  input  l1,
  input  l2,
  input  l3,
  input  l4,
  input  l5,
  input  l6,
  input  l7,
  input  l8,
  input  l9,
  input  l10,
  input  l11,
  input  l12,
  input  l13,
  input  l14,
  input  l15,
  input  in_17,
  input  in_18,
  input  in_19,
  input  in_20,
  output out_21
);

  wire mux8_1_out_12, mux8_2_out_12;

  mux8 mux8_1 (
    .l0(l0), .l1(l1), .l2(l2), .l3(l3), .l4(l4), .l5(l5), .l6(l6), .l7(l7), .in_9(in_18), .in_10(in_19),
    .in_11(in_20), .out_12(mux8_1_out_12));
  mux8 mux8_2 (
    .l0(l8), .l1(l9), .l2(l10), .l3(l11), .l4(l12), .l5(l13), .l6(l14), .l7(l15), .in_9(in_18),
    .in_10(in_19), .in_11(in_20), .out_12(mux8_2_out_12));
  mux2 mux2_1 (.A(mux8_1_out_12), .B(mux8_2_out_12), .Sel(in_17), .S(out_21));
endmodule

module mux16b (
  input  l0,
  input  l1,
  input  l2,
  input  l3,
  input  l4,
  input  l5,
  input  l6,
  input  l7,
  input  l8,
  input  l9,
  input  l10,
  input  l11,
  input  l12,
  input  l13,
  input  l14,
  input  l15,
  input  [3:0] in_17,
  output out_18
);

  wire mux8_1_out_12, mux8_2_out_12;

  mux8 mux8_1 (
    .l0(l0), .l1(l1), .l2(l2), .l3(l3), .l4(l4), .l5(l5), .l6(l6), .l7(l7), .in_9(in_17[2]),
    .in_10(in_17[1]), .in_11(in_17[0]), .out_12(mux8_1_out_12));
  mux8 mux8_2 (
    .l0(l8), .l1(l9), .l2(l10), .l3(l11), .l4(l12), .l5(l13), .l6(l14), .l7(l15), .in_9(in_17[2]),
    .in_10(in_17[1]), .in_11(in_17[0]), .out_12(mux8_2_out_12));
  mux2 mux2_1 (.A(mux8_1_out_12), .B(mux8_2_out_12), .Sel(in_17[3]), .S(out_18));
endmodule

module mux32 (
  input  l0,
  input  l1,
  input  l2,
  input  l3,
  input  l4,
  input  l5,
  input  l6,
  input  l7,
  input  l8,
  input  l9,
  input  l10,
  input  l11,
  input  l12,
  input  l13,
  input  l14,
  input  l15,
  input  l16,
  input  l17,
  input  l18,
  input  l19,
  input  l20,
  input  l21,
  input  l22,
  input  l23,
  input  l24,
  input  l25,
  input  l26,
  input  l27,
  input  l28,
  input  l29,
  input  l30,
  input  sel5,
  input  sel3,
  input  sel2,
  input  sel1,
  input  sel0,
  input  l31,
  output out_38
);

  wire mux16_1_out_21, mux16_2_out_21;

  mux16 mux16_1 (
    .l0(l0), .l1(l1), .l2(l2), .l3(l3), .l4(l4), .l5(l5), .l6(l6), .l7(l7), .l8(l8), .l9(l9), .l10(l10),
    .l11(l11), .l12(l12), .l13(l13), .l14(l14), .l15(l15), .in_17(sel3), .in_18(sel2), .in_19(sel1),
    .in_20(sel0), .out_21(mux16_1_out_21));
  mux16 mux16_2 (
    .l0(l16), .l1(l17), .l2(l18), .l3(l19), .l4(l20), .l5(l21), .l6(l22), .l7(l23), .l8(l24), .l9(l25),
    .l10(l26), .l11(l27), .l12(l28), .l13(l29), .l14(l30), .l15(l31), .in_17(sel3), .in_18(sel2),
    .in_19(sel1), .in_20(sel0), .out_21(mux16_2_out_21));
  mux2 mux2_1 (.A(mux16_1_out_21), .B(mux16_2_out_21), .Sel(sel5), .S(out_38));
endmodule

module mux32b (
  input  l0,
  input  l1,
  input  l2,
  input  l3,
  input  l4,
  input  l5,
  input  l6,
  input  l7,
  input  l8,
  input  l9,
  input  l10,
  input  l11,
  input  l12,
  input  l13,
  input  l14,
  input  l15,
  input  l16,
  input  l17,
  input  l18,
  input  l19,
  input  l20,
  input  l21,
  input  l22,
  input  l23,
  input  l24,
  input  l25,
  input  l26,
  input  l27,
  input  l28,
  input  l29,
  input  l30,
  input  l31,
  input  [4:0] in_33,
  output out_34
);

  wire mux16_1_out_21, mux16_2_out_21;

  mux16 mux16_1 (
    .l0(l0), .l1(l1), .l2(l2), .l3(l3), .l4(l4), .l5(l5), .l6(l6), .l7(l7), .l8(l8), .l9(l9), .l10(l10),
    .l11(l11), .l12(l12), .l13(l13), .l14(l14), .l15(l15), .in_17(in_33[3]), .in_18(in_33[2]),
    .in_19(in_33[1]), .in_20(in_33[0]), .out_21(mux16_1_out_21));
  mux16 mux16_2 (
    .l0(l16), .l1(l17), .l2(l18), .l3(l19), .l4(l20), .l5(l21), .l6(l22), .l7(l23), .l8(l24), .l9(l25),
    .l10(l26), .l11(l27), .l12(l28), .l13(l29), .l14(l30), .l15(l31), .in_17(in_33[3]), .in_18(in_33[2]),
    .in_19(in_33[1]), .in_20(in_33[0]), .out_21(mux16_2_out_21));
  mux2 mux2_1 (.A(mux16_1_out_21), .B(mux16_2_out_21), .Sel(in_33[4]), .S(out_34));
endmodule

module SubFULL (
  input  A,
  input  B,
  input  Bin,
  output d,
  output b_2
);

  wire and_1_out, and_2_out, xor_1_out;

  xor xor_1 (xor_1_out, A, B);
  xor xor_2 (d, xor_1_out, Bin);
  and and_1 (and_1_out, ~xor_1_out, Bin);  // AND_Gate
  and and_2 (and_2_out, ~A, B);  // AND_Gate
  or or_1 (b_2, and_1_out, and_2_out);
endmodule

module Fullsubtractor (
  input  V1,
  input  B,
  input  A,
  output out_4,
  output out_5
);

  wire and_1_out, and_2_out, and_3_out, and_4_out, and_5_out, and_6_out, and_7_out;

  and and_1 (and_1_out, ~A, ~B, V1);  // AND_Gate
  and and_2 (and_2_out, ~A, B, ~V1);  // AND_Gate
  and and_3 (and_3_out, A, ~B, ~V1);  // AND_Gate
  and and_4 (and_4_out, A, B, V1);
  and and_5 (and_5_out, ~A, V1);  // AND_Gate
  and and_6 (and_6_out, ~A, B);  // AND_Gate
  and and_7 (and_7_out, B, V1);
  or or_1 (out_4, and_1_out, and_2_out, and_3_out, and_4_out);
  or or_2 (out_5, and_5_out, and_6_out, and_7_out);
endmodule

module FullSubtratctor32bit (
  input  [31:0] V1,
  input  [31:0] B,
  input  [31:0] A,
  output [31:0] out_4,
  output [31:0] out_5
);

  wire [31:0] and_1_out, and_2_out, and_3_out, and_4_out, and_5_out, and_6_out, and_7_out;

  assign and_1_out = ~A & ~B & V1;  // AND_Gate and_1, 32 bits wide
  assign and_2_out = ~A & B & ~V1;  // AND_Gate and_2, 32 bits wide
  assign and_3_out = A & ~B & ~V1;  // AND_Gate and_3, 32 bits wide
  assign and_4_out = A & B & V1;  // AND_Gate and_4, 32 bits wide
  assign and_5_out = ~A & V1;  // AND_Gate and_5, 32 bits wide
  assign and_6_out = ~A & B;  // AND_Gate and_6, 32 bits wide
  assign and_7_out = B & V1;  // AND_Gate and_7, 32 bits wide
  assign out_4 = and_1_out | and_2_out | and_3_out | and_4_out;  // OR_Gate or_1, 32 bits wide
  assign out_5 = and_5_out | and_6_out | and_7_out;  // OR_Gate or_2, 32 bits wide
endmodule

module FullAdder (
  input  vem1,
  input  B,
  input  A,
  output soma,
  output vai1
);

  wire and_1_out, and_2_out, and_3_out, and_4_out, or_1_out, xnor_1_out, xor_1_out;

  xnor xnor_1 (xnor_1_out, B, A);
  xor xor_1 (xor_1_out, B, A);
  or or_1 (or_1_out, B, A);
  and and_1 (and_1_out, B, A);
  and and_2 (and_2_out, or_1_out, vem1);
  and and_3 (and_3_out, xnor_1_out, vem1);
  and and_4 (and_4_out, xor_1_out, ~vem1);  // AND_Gate
  or or_2 (vai1, and_1_out, and_2_out);
  or or_3 (soma, and_3_out, and_4_out);
endmodule

module FullAdder4bits (
  input  [3:0] vem1,
  input  [3:0] B,
  input  [3:0] A,
  output [3:0] soma,
  output [3:0] vai1
);

  wire [3:0] and_1_out, and_2_out, and_3_out, and_4_out, or_1_out, xnor_1_out, xor_1_out;

  Hex_Digit_Display hex_digit_display_1 (.value(vem1));  // open: dp
  Hex_Digit_Display hex_digit_display_2 (.value(A));  // open: dp
  Hex_Digit_Display hex_digit_display_3 (.value(B));  // open: dp
  assign xnor_1_out = ~(B ^ A);  // XNOR_Gate xnor_1, 4 bits wide
  assign xor_1_out = B ^ A;  // XOR_Gate xor_1, 4 bits wide
  assign or_1_out = B | A;  // OR_Gate or_1, 4 bits wide
  assign and_1_out = B & A;  // AND_Gate and_1, 4 bits wide
  assign and_2_out = or_1_out & vem1;  // AND_Gate and_2, 4 bits wide
  assign and_3_out = xnor_1_out & vem1;  // AND_Gate and_3, 4 bits wide
  assign and_4_out = xor_1_out & ~vem1;  // AND_Gate and_4, 4 bits wide
  assign vai1 = and_1_out | and_2_out;  // OR_Gate or_2, 4 bits wide
  Hex_Digit_Display hex_digit_display_4 (.value(soma));  // open: dp
  assign soma = and_3_out | and_4_out;  // OR_Gate or_3, 4 bits wide
  Hex_Digit_Display hex_digit_display_5 (.value(vai1));  // open: dp
endmodule

module ULACell_DeuErro (
  input  b,
  input  a,
  input  vem1,
  input  bin,
  input  [4:0] OpCode,
  output saida,
  output vai1,
  output b_2
);

  wire and_1_out, fulladder_1_soma, nand_1_out, nor_1_out, not_1_out, not_2_out, not_3_out, not_4_out,
       or_1_out, subfull_1_d, xnor_1_out, xor_1_out;

  and and_1 (and_1_out, b, a);
  or or_1 (or_1_out, b, a);
  FullAdder fulladder_1 (.B(b), .A(a), .vem1(vem1), .vai1(vai1), .soma(fulladder_1_soma));
  xor xor_1 (xor_1_out, b, a);
  SubFULL subfull_1 (.A(a), .B(b), .Bin(bin), .d(subfull_1_d), .b_2(b_2));
  not not_1 (not_1_out, fulladder_1_soma);
  not not_2 (not_2_out, b_2);
  nand nand_1 (nand_1_out, b, a);
  nor nor_1 (nor_1_out, b, a);
  xnor xnor_1 (xnor_1_out, b, a);
  not not_3 (not_3_out, a);
  not not_4 (not_4_out, b);
  mux32b mux32b_1 (
    .l0(and_1_out), .l1(or_1_out), .l2(fulladder_1_soma), .l3(xor_1_out), .l4(a), .l5(b), .l6(a), .l7(b),
    .l8(a), .l9(b), .l10(a), .l11(b), .l12(subfull_1_d), .l13(nand_1_out), .l14(nor_1_out), .l15(xnor_1_out),
    .l16(not_3_out), .l17(not_4_out), .l18(not_1_out), .l19(not_2_out), .l20(a), .l21(b), .in_33(OpCode),
    .out_34(saida));  // open: l22, l23, l24, l25, l26, l27, l28, l29, l30, l31

  // Notes on the sheet:
  //   00000 - AND
  //   00001 - OR
  //   00011 - XOR
  //   01110 - NOR
  //   10100 - A
  //   10101 - B
  //   00010 - SOMADOR
  //   00100 - SLL A
  //   00101 - SLL B
  //   00110 - SRL A
  //   00111 - SRL B
  //   01000 - SLA A
  //   01001 - SLA B
  //   01010 - SRA A
  //   01011 - SRA B
  //   01100 - SUBTRACTOR
  //   01101 - NAND
  //   01111 - XNOR
  //   10000 - NOT A
  //   10001 - NOT B
  //   10010 - NOT A+B
  //   10011 - NOT A-B
endmodule

module Ulacell (
  input  a,
  input  b,
  input  vem1,
  input  [4:0] OpCode,
  input  in_5,
  output saida,
  output vai1
);

  wire and_1_out, fulladder_1_soma, mux2_1_s, nand_1_out, nand_2_out, nor_1_out, not_1_out, not_2_out,
       not_3_out, not_4_out, or_1_out, xnor_1_out, xor_1_out;

  and and_1 (and_1_out, a, a);
  or or_1 (or_1_out, a, a);
  FullAdder fulladder_1 (.B(a), .A(a), .vem1(vem1), .vai1(vai1), .soma(fulladder_1_soma));
  xor xor_1 (xor_1_out, a, a);
  not not_1 (not_1_out, a);
  not not_2 (not_2_out, fulladder_1_soma);
  nand nand_1 (nand_1_out, a, a);
  nor nor_1 (nor_1_out, a, a);
  xnor xnor_1 (xnor_1_out, a, a);
  not not_3 (not_3_out, a);
  not not_4 (not_4_out, a);
  nand nand_2 (nand_2_out, ~a, a);  // NAND_Gate
  mux2 mux2_1 (.A(a), .B(not_1_out), .Sel(in_5), .S(mux2_1_s));
  mux32b mux32b_1 (
    .l0(and_1_out), .l1(or_1_out), .l2(fulladder_1_soma), .l3(xor_1_out), .l4(a), .l5(a), .l6(a), .l7(a),
    .l8(a), .l9(a), .l10(a), .l11(a), .l12(nand_1_out), .l13(nor_1_out), .l14(xnor_1_out), .l15(not_3_out),
    .l16(not_4_out), .l17(not_2_out), .l18(a), .l19(a), .l31(nand_2_out), .in_33(OpCode), .out_34(saida));  // open: l20, l21, l22, l23, l24, l25, l26, l27, l28, l29, l30

  assign b = a;

  // Notes on the sheet:
  //   00000 - AND
  //   00001 - OR
  //   00010 - SOMADOR
  //   00011 - XOR
  //   00100 - SLL A
  //   00101 - SLL B
  //   00110 - SRL A
  //   00111 - SRL B
  //   01000 - SLA A
  //   01001 - SLA B
  //   01010 - SRA A
  //   01011 - SRA B
  //   01100 - NAND
  //   01101 - NOR
  //   01110 - XNOR
  //   01111 - NOT B
  //   10000 - NOT A
  //   10001 - NOT A+B
  //   10010 - B
  //   10011 - A
  //   10100 - A AND NOT B
  //   10101 - NOT A AND B
  //   10110 - NOT A AND NOT B
endmodule

module ShiftLeftLogical32bit (
  input  [31:0] in_1,
  input  Shift,
  output [31:0] out_3
);

  mux2b mux2b_1 (.A(in_1), .B({in_1[30:0], 1'b0}), .Sel(Shift), .S(out_3));
endmodule

module ShiftLeftArith32bit (
  input  [31:0] in_1,
  input  Shift,
  output [31:0] out_3
);

  mux2b mux2b_1 (.A(in_1), .B({in_1[30:0], in_1[0]}), .Sel(Shift), .S(out_3));
endmodule

module ShiftRightLogical32bit (
  input  [31:0] in_1,
  input  Shift,
  output [31:0] out_3
);

  mux2b mux2b_1 (.A(in_1), .B({1'b0, in_1[31:1]}), .Sel(Shift), .S(out_3));
endmodule

module ShiftRightArith32bit (
  input  [31:0] in_1,
  input  Shift,
  output [31:0] out_3
);

  mux2b mux2b_1 (.A(in_1), .B({{2{in_1[31]}}, in_1[30:1]}), .Sel(Shift), .S(out_3));
endmodule

module SLLDetect (
  input  [4:0] ALUOpCode,
  output sll
);

  and and_1 (sll, ~ALUOpCode[0], ~ALUOpCode[1], ~ALUOpCode[2], ~ALUOpCode[3], ALUOpCode[4]);  // AND_Gate
endmodule

module SLLADetector (
  input  [4:0] UlaOpCode,
  output out_2
);

  and and_1 (out_2, ~UlaOpCode[0], ~UlaOpCode[1], UlaOpCode[2], ~UlaOpCode[3], ~UlaOpCode[4]);  // AND_Gate
endmodule

module SLLBDetector (
  input  [4:0] UlaOpCode,
  output saida
);

  and and_1 (saida, ~UlaOpCode[4], ~UlaOpCode[3], UlaOpCode[2], ~UlaOpCode[1], UlaOpCode[0]);  // AND_Gate
endmodule

module SRLADetector (
  input  [4:0] UlaOpCode,
  output out_2
);

  and and_1 (out_2, ~UlaOpCode[0], UlaOpCode[1], UlaOpCode[2], ~UlaOpCode[3], ~UlaOpCode[4]);  // AND_Gate
endmodule

module SRLBDetector (
  input  [4:0] UlaOpCode,
  output out_2
);

  and and_1 (out_2, ~UlaOpCode[4], ~UlaOpCode[3], UlaOpCode[2], UlaOpCode[1], UlaOpCode[0]);  // AND_Gate
endmodule

module SLAADetector (
  input  [4:0] UlaOpCode,
  output out_2
);

  and and_1 (out_2, ~UlaOpCode[4], UlaOpCode[3], ~UlaOpCode[2], ~UlaOpCode[1], ~UlaOpCode[0]);  // AND_Gate
endmodule

module SLABDetector (
  input  [4:0] UlaOpCode,
  output out_2
);

  and and_1 (out_2, ~UlaOpCode[4], UlaOpCode[3], ~UlaOpCode[2], ~UlaOpCode[1], UlaOpCode[0]);  // AND_Gate
endmodule

module SRAADetector (
  input  [4:0] UlaOpCode,
  output out_2
);

  and and_1 (out_2, ~UlaOpCode[4], UlaOpCode[3], ~UlaOpCode[2], UlaOpCode[1], ~UlaOpCode[0]);  // AND_Gate
endmodule

module SRABDetector (
  input  [4:0] UlaOpCode,
  output out_2
);

  and and_1 (out_2, ~UlaOpCode[4], UlaOpCode[3], ~UlaOpCode[2], UlaOpCode[1], UlaOpCode[0]);  // AND_Gate
endmodule

module ULA_DeuErro (
  input  [31:0] B,
  input  [31:0] A,
  input  [4:0] ULAOpCode,
  output out_4,
  output [31:0] R
);

  wire slaadetector_1_out_2, slabdetector_1_out_2, slladetector_1_out_2, sllbdetector_1_saida,
       sraadetector_1_out_2, srabdetector_1_out_2, srladetector_1_out_2, srlbdetector_1_out_2, ulacell_1_p1,
       ulacell_1_p6, ulacell_3_p7, ulacell_4_p2, ulacell_4_p7, ulacell_6_p7, ulacell_7_p7, ulacell_8_p7,
       ulacell_9_p2, ulacell_9_p7, ulacell_11_p7, ulacell_12_p2, ulacell_12_p7, ulacell_14_p7, ulacell_15_p7,
       ulacell_16_p7, ulacell_17_p2, ulacell_17_p7, ulacell_19_p7, ulacell_20_p2, ulacell_20_p7,
       ulacell_22_p7, ulacell_23_p7, ulacell_24_p7, ulacell_25_p7, ulacell_26_p7, ulacell_27_p7,
       ulacell_28_p7, ulacell_29_p7, ulacell_30_p7, ulacell_31_p7;
  wire [30:0] shiftrightarith32bit_1_out_3;
  wire [31:0] shiftleftarith32bit_1_out_3, shiftleftarith32bit_2_out_3, shiftleftlogical32bit_1_out_3,
       shiftleftlogical32bit_2_out_3, shiftrightlogical32bit_1_out_3, shiftrightlogical32bit_2_out_3;
  wire [31:30] shiftrightarith32bit_2_out_3;

  ShiftLeftLogical32bit shiftleftlogical32bit_1 (
    .in_1(B), .Shift(sllbdetector_1_saida), .out_3(shiftleftlogical32bit_1_out_3));
  SLLBDetector sllbdetector_1 (.saida(sllbdetector_1_saida), .UlaOpCode(ULAOpCode));
  ShiftLeftLogical32bit shiftleftlogical32bit_2 (
    .in_1(A), .Shift(slladetector_1_out_2), .out_3(shiftleftlogical32bit_2_out_3));
  SLLADetector slladetector_1 (.out_2(slladetector_1_out_2), .UlaOpCode(ULAOpCode));
  SRLADetector srladetector_1 (.out_2(srladetector_1_out_2), .UlaOpCode(ULAOpCode));
  ShiftRightLogical32bit shiftrightlogical32bit_1 (
    .in_1(shiftleftlogical32bit_1_out_3), .Shift(srlbdetector_1_out_2), .out_3(shiftrightlogical32bit_1_out_3));
  ShiftLeftArith32bit shiftleftarith32bit_1 (
    .in_1(shiftrightlogical32bit_1_out_3), .Shift(slabdetector_1_out_2), .out_3(shiftleftarith32bit_1_out_3));
  SRLBDetector srlbdetector_1 (.out_2(srlbdetector_1_out_2), .UlaOpCode(ULAOpCode));
  SLABDetector slabdetector_1 (.out_2(slabdetector_1_out_2), .UlaOpCode(ULAOpCode));
  ShiftRightLogical32bit shiftrightlogical32bit_2 (
    .in_1(shiftleftlogical32bit_2_out_3), .Shift(srladetector_1_out_2), .out_3(shiftrightlogical32bit_2_out_3));
  SLAADetector slaadetector_1 (.out_2(slaadetector_1_out_2), .UlaOpCode(ULAOpCode));
  ShiftRightArith32bit shiftrightarith32bit_1 (
    .in_1(shiftleftarith32bit_1_out_3), .Shift(srabdetector_1_out_2),
    .out_3({shiftrightarith32bit_2_out_3[30], shiftrightarith32bit_1_out_3}));
  SRABDetector srabdetector_1 (.out_2(srabdetector_1_out_2), .UlaOpCode(ULAOpCode));
  ShiftRightArith32bit shiftrightarith32bit_2 (
    .in_1(shiftleftarith32bit_2_out_3), .Shift(sraadetector_1_out_2),
    .out_3({shiftrightarith32bit_2_out_3, {30{shiftrightarith32bit_2_out_3[30]}}}));
  ShiftLeftArith32bit shiftleftarith32bit_2 (
    .in_1(shiftrightlogical32bit_2_out_3), .Shift(slaadetector_1_out_2), .out_3(shiftleftarith32bit_2_out_3));
  SRAADetector sraadetector_1 (.out_2(sraadetector_1_out_2), .UlaOpCode(ULAOpCode));
  // Ulacell ulacell_1: pin names not known; wires that end beside it: ulacell_1_p1, shiftrightarith32bit_2_out_3[30], ULAOpCode, shiftrightarith32bit_1_out_3[30], R[30], ulacell_1_p6
  // Ulacell ulacell_2: pin names not known; wires that end beside it: out_4, shiftrightarith32bit_2_out_3[31], ULAOpCode, shiftrightarith32bit_2_out_3[30], R[31], ulacell_1_p1
  // Ulacell ulacell_3: pin names not known; wires that end beside it: shiftrightarith32bit_1_out_3[30], ulacell_1_p6, shiftrightarith32bit_2_out_3[30], ULAOpCode, shiftrightarith32bit_1_out_3[29], R[29], ulacell_3_p7
  // Ulacell ulacell_4: pin names not known; wires that end beside it: shiftrightarith32bit_1_out_3[28], ulacell_4_p2, shiftrightarith32bit_2_out_3[30], ULAOpCode, shiftrightarith32bit_1_out_3[27], R[27], ulacell_4_p7
  // Ulacell ulacell_5: pin names not known; wires that end beside it: shiftrightarith32bit_1_out_3[29], ulacell_3_p7, shiftrightarith32bit_2_out_3[30], ULAOpCode, shiftrightarith32bit_1_out_3[28], R[28], ulacell_4_p2
  // Ulacell ulacell_6: pin names not known; wires that end beside it: shiftrightarith32bit_1_out_3[27], ulacell_4_p7, shiftrightarith32bit_2_out_3[30], ULAOpCode, shiftrightarith32bit_1_out_3[26], R[26], ulacell_6_p7
  // Ulacell ulacell_7: pin names not known; wires that end beside it: shiftrightarith32bit_1_out_3[26], ulacell_6_p7, shiftrightarith32bit_2_out_3[30], ULAOpCode, shiftrightarith32bit_1_out_3[25], R[25], ulacell_7_p7
  // Ulacell ulacell_8: pin names not known; wires that end beside it: shiftrightarith32bit_1_out_3[25], ulacell_7_p7, shiftrightarith32bit_2_out_3[30], ULAOpCode, shiftrightarith32bit_1_out_3[24], R[24], ulacell_8_p7
  // Ulacell ulacell_9: pin names not known; wires that end beside it: shiftrightarith32bit_1_out_3[23], ulacell_9_p2, shiftrightarith32bit_2_out_3[30], ULAOpCode, shiftrightarith32bit_1_out_3[22], R[22], ulacell_9_p7
  // Ulacell ulacell_10: pin names not known; wires that end beside it: shiftrightarith32bit_1_out_3[24], ulacell_8_p7, shiftrightarith32bit_2_out_3[30], ULAOpCode, shiftrightarith32bit_1_out_3[23], R[23], ulacell_9_p2
  // Ulacell ulacell_11: pin names not known; wires that end beside it: shiftrightarith32bit_1_out_3[22], ulacell_9_p7, shiftrightarith32bit_2_out_3[30], ULAOpCode, shiftrightarith32bit_1_out_3[21], R[21], ulacell_11_p7
  // Ulacell ulacell_12: pin names not known; wires that end beside it: shiftrightarith32bit_1_out_3[20], ulacell_12_p2, shiftrightarith32bit_2_out_3[30], ULAOpCode, shiftrightarith32bit_1_out_3[19], R[19], ulacell_12_p7
  // Ulacell ulacell_13: pin names not known; wires that end beside it: shiftrightarith32bit_1_out_3[21], ulacell_11_p7, shiftrightarith32bit_2_out_3[30], ULAOpCode, shiftrightarith32bit_1_out_3[20], R[20], ulacell_12_p2
  // Ulacell ulacell_14: pin names not known; wires that end beside it: shiftrightarith32bit_1_out_3[19], ulacell_12_p7, shiftrightarith32bit_2_out_3[30], ULAOpCode, shiftrightarith32bit_1_out_3[18], R[18], ulacell_14_p7
  // Ulacell ulacell_15: pin names not known; wires that end beside it: shiftrightarith32bit_1_out_3[18], ulacell_14_p7, shiftrightarith32bit_2_out_3[30], ULAOpCode, shiftrightarith32bit_1_out_3[17], R[17], ulacell_15_p7
  // Ulacell ulacell_16: pin names not known; wires that end beside it: shiftrightarith32bit_1_out_3[17], ulacell_15_p7, shiftrightarith32bit_2_out_3[30], ULAOpCode, shiftrightarith32bit_1_out_3[16], R[16], ulacell_16_p7
  // Ulacell ulacell_17: pin names not known; wires that end beside it: shiftrightarith32bit_1_out_3[15], ulacell_17_p2, shiftrightarith32bit_2_out_3[30], ULAOpCode, shiftrightarith32bit_1_out_3[14], R[14], ulacell_17_p7
  // Ulacell ulacell_18: pin names not known; wires that end beside it: shiftrightarith32bit_1_out_3[16], ulacell_16_p7, shiftrightarith32bit_2_out_3[30], ULAOpCode, shiftrightarith32bit_1_out_3[15], R[15], ulacell_17_p2
  // Ulacell ulacell_19: pin names not known; wires that end beside it: shiftrightarith32bit_1_out_3[14], ulacell_17_p7, shiftrightarith32bit_2_out_3[30], ULAOpCode, shiftrightarith32bit_1_out_3[13], R[13], ulacell_19_p7
  // Ulacell ulacell_20: pin names not known; wires that end beside it: shiftrightarith32bit_1_out_3[12], ulacell_20_p2, shiftrightarith32bit_2_out_3[30], ULAOpCode, shiftrightarith32bit_1_out_3[11], R[11], ulacell_20_p7
  // Ulacell ulacell_21: pin names not known; wires that end beside it: shiftrightarith32bit_1_out_3[13], ulacell_19_p7, shiftrightarith32bit_2_out_3[30], ULAOpCode, shiftrightarith32bit_1_out_3[12], R[12], ulacell_20_p2
  // Ulacell ulacell_22: pin names not known; wires that end beside it: shiftrightarith32bit_1_out_3[11], ulacell_20_p7, shiftrightarith32bit_2_out_3[30], ULAOpCode, shiftrightarith32bit_1_out_3[10], R[10], ulacell_22_p7
  // Ulacell ulacell_23: pin names not known; wires that end beside it: shiftrightarith32bit_1_out_3[10], ulacell_22_p7, shiftrightarith32bit_2_out_3[30], ULAOpCode, shiftrightarith32bit_1_out_3[9], R[9], ulacell_23_p7
  // Ulacell ulacell_24: pin names not known; wires that end beside it: shiftrightarith32bit_1_out_3[9], ulacell_23_p7, shiftrightarith32bit_2_out_3[30], ULAOpCode, shiftrightarith32bit_1_out_3[8], R[8], ulacell_24_p7
  // Ulacell ulacell_25: pin names not known; wires that end beside it: shiftrightarith32bit_1_out_3[8], ulacell_24_p7, shiftrightarith32bit_2_out_3[30], ULAOpCode, shiftrightarith32bit_1_out_3[7], R[7], ulacell_25_p7
  // Ulacell ulacell_26: pin names not known; wires that end beside it: shiftrightarith32bit_1_out_3[7], ulacell_25_p7, shiftrightarith32bit_2_out_3[30], ULAOpCode, shiftrightarith32bit_1_out_3[6], R[6], ulacell_26_p7
  // Ulacell ulacell_27: pin names not known; wires that end beside it: shiftrightarith32bit_1_out_3[6], ulacell_26_p7, shiftrightarith32bit_2_out_3[30], ULAOpCode, shiftrightarith32bit_1_out_3[5], R[5], ulacell_27_p7
  // Ulacell ulacell_28: pin names not known; wires that end beside it: shiftrightarith32bit_1_out_3[5], ulacell_27_p7, shiftrightarith32bit_2_out_3[30], ULAOpCode, shiftrightarith32bit_1_out_3[4], R[4], ulacell_28_p7
  // Ulacell ulacell_29: pin names not known; wires that end beside it: shiftrightarith32bit_1_out_3[4], ulacell_28_p7, shiftrightarith32bit_2_out_3[30], ULAOpCode, shiftrightarith32bit_1_out_3[3], R[3], ulacell_29_p7
  // Ulacell ulacell_30: pin names not known; wires that end beside it: shiftrightarith32bit_1_out_3[3], ulacell_29_p7, shiftrightarith32bit_2_out_3[30], ULAOpCode, shiftrightarith32bit_1_out_3[2], R[2], ulacell_30_p7
  // Ulacell ulacell_31: pin names not known; wires that end beside it: shiftrightarith32bit_1_out_3[2], ulacell_30_p7, shiftrightarith32bit_2_out_3[30], ULAOpCode, shiftrightarith32bit_1_out_3[1], R[1], ulacell_31_p7
  // Ulacell ulacell_32: pin names not known; wires that end beside it: shiftrightarith32bit_1_out_3[1], ulacell_31_p7, shiftrightarith32bit_2_out_3[30], ULAOpCode, shiftrightarith32bit_1_out_3[0], R[0], 1'b0

  // Notes on the sheet:
  //   00001 - OR
  //   10010 - A
  //   10011 - B
  //   00000 - AND
  //   00010 - SOMADOR
  //   00011 - XOR
  //   00100 - SLL A
  //   00101 - SLL B
  //   00110 - SRL A
  //   00111 - SRL B
  //   01000 - SLA A
  //   01001 - SLA B
  //   01010 - SRA A
  //   01011 - SRA B
  //   01100 - NAND
  //   01101 - NOR
  //   01110 - XNOR
  //   01111 - NOT A
  //   10000 - NOT B
  //   10001 - NOT A+B
endmodule

module Ulafinal (
  input  [31:0] A,
  input  [31:0] B,
  input  [4:0] ULA_OpCode,
  output out_4,
  output out_5,
  output [31:0] Out
);

  wire slaadetector_1_out_2, slabdetector_1_out_2, slladetector_1_out_2, sllbdetector_1_saida,
       sraadetector_1_out_2, srabdetector_1_out_2, srladetector_1_out_2, srlbdetector_1_out_2, ulacell_1_p6,
       ulacell_2_p7, ulacell_3_p7, ulacell_4_p2, ulacell_4_p7, ulacell_6_p7, ulacell_7_p7, ulacell_8_p7,
       ulacell_9_p7, ulacell_10_p7, ulacell_11_p7, ulacell_12_p7, ulacell_13_p7, ulacell_14_p2,
       ulacell_14_p7, ulacell_16_p7, ulacell_17_p2, ulacell_17_p7, ulacell_19_p7, ulacell_20_p2,
       ulacell_20_p7, ulacell_22_p2, ulacell_22_p7, ulacell_24_p7, ulacell_25_p2, ulacell_25_p7,
       ulacell_27_p7, ulacell_28_p7, ulacell_29_p7, ulacell_30_p2, ulacell_30_p7;
  wire [31:0] shiftleftarith32bit_1_out_3, shiftleftarith32bit_2_out_3, shiftleftlogical32bit_1_out_3,
       shiftleftlogical32bit_2_out_3, shiftrightarith32bit_1_out_3, shiftrightarith32bit_2_out_3,
       shiftrightlogical32bit_1_out_3, shiftrightlogical32bit_2_out_3;

  ShiftLeftLogical32bit shiftleftlogical32bit_1 (
    .in_1(A), .Shift(slladetector_1_out_2), .out_3(shiftleftlogical32bit_1_out_3));
  SLLADetector slladetector_1 (.out_2(slladetector_1_out_2), .UlaOpCode(ULA_OpCode));
  ShiftLeftLogical32bit shiftleftlogical32bit_2 (
    .in_1(B), .Shift(sllbdetector_1_saida), .out_3(shiftleftlogical32bit_2_out_3));
  SRLBDetector srlbdetector_1 (.out_2(srlbdetector_1_out_2), .UlaOpCode(ULA_OpCode));
  SLLBDetector sllbdetector_1 (.saida(sllbdetector_1_saida), .UlaOpCode(ULA_OpCode));
  ShiftRightLogical32bit shiftrightlogical32bit_1 (
    .in_1(shiftleftlogical32bit_1_out_3), .Shift(srladetector_1_out_2), .out_3(shiftrightlogical32bit_1_out_3));
  SRLADetector srladetector_1 (.out_2(srladetector_1_out_2), .UlaOpCode(ULA_OpCode));
  SLAADetector slaadetector_1 (.out_2(slaadetector_1_out_2), .UlaOpCode(ULA_OpCode));
  ShiftLeftArith32bit shiftleftarith32bit_1 (
    .in_1(shiftrightlogical32bit_2_out_3), .Shift(slabdetector_1_out_2), .out_3(shiftleftarith32bit_1_out_3));
  ShiftRightLogical32bit shiftrightlogical32bit_2 (
    .in_1(shiftleftlogical32bit_2_out_3), .Shift(srlbdetector_1_out_2), .out_3(shiftrightlogical32bit_2_out_3));
  SLABDetector slabdetector_1 (.out_2(slabdetector_1_out_2), .UlaOpCode(ULA_OpCode));
  ShiftRightArith32bit shiftrightarith32bit_1 (
    .in_1(shiftleftarith32bit_2_out_3), .Shift(sraadetector_1_out_2), .out_3(shiftrightarith32bit_1_out_3));
  ShiftLeftArith32bit shiftleftarith32bit_2 (
    .in_1(shiftrightlogical32bit_1_out_3), .Shift(slaadetector_1_out_2), .out_3(shiftleftarith32bit_2_out_3));
  SRAADetector sraadetector_1 (.out_2(sraadetector_1_out_2), .UlaOpCode(ULA_OpCode));
  ShiftRightArith32bit shiftrightarith32bit_2 (
    .in_1(shiftleftarith32bit_1_out_3), .Shift(srabdetector_1_out_2), .out_3(shiftrightarith32bit_2_out_3));
  SRABDetector srabdetector_1 (.out_2(srabdetector_1_out_2), .UlaOpCode(ULA_OpCode));
  // Ulacell ulacell_1: pin names not known; wires that end beside it: out_5, shiftrightarith32bit_2_out_3[31], ULA_OpCode, shiftrightarith32bit_1_out_3[31], Out[31], ulacell_1_p6
  // Ulacell ulacell_2: pin names not known; wires that end beside it: shiftrightarith32bit_1_out_3[31], ulacell_1_p6, shiftrightarith32bit_2_out_3[30], ULA_OpCode, shiftrightarith32bit_1_out_3[30], Out[30], ulacell_2_p7
  // Ulacell ulacell_3: pin names not known; wires that end beside it: shiftrightarith32bit_1_out_3[30], ulacell_2_p7, shiftrightarith32bit_2_out_3[29], ULA_OpCode, shiftrightarith32bit_1_out_3[29], Out[29], ulacell_3_p7
  // Ulacell ulacell_4: pin names not known; wires that end beside it: shiftrightarith32bit_1_out_3[28], ulacell_4_p2, shiftrightarith32bit_2_out_3[27], ULA_OpCode, shiftrightarith32bit_1_out_3[27], Out[27], ulacell_4_p7
  // Ulacell ulacell_5: pin names not known; wires that end beside it: shiftrightarith32bit_1_out_3[29], ulacell_3_p7, shiftrightarith32bit_2_out_3[28], ULA_OpCode, shiftrightarith32bit_1_out_3[28], Out[28], ulacell_4_p2
  // Ulacell ulacell_6: pin names not known; wires that end beside it: shiftrightarith32bit_1_out_3[27], ulacell_4_p7, shiftrightarith32bit_2_out_3[26], ULA_OpCode, shiftrightarith32bit_1_out_3[26], Out[26], ulacell_6_p7
  // Ulacell ulacell_7: pin names not known; wires that end beside it: shiftrightarith32bit_1_out_3[26], ulacell_6_p7, shiftrightarith32bit_2_out_3[25], ULA_OpCode, shiftrightarith32bit_1_out_3[25], Out[25], ulacell_7_p7
  // Ulacell ulacell_8: pin names not known; wires that end beside it: shiftrightarith32bit_1_out_3[25], ulacell_7_p7, shiftrightarith32bit_2_out_3[24], ULA_OpCode, shiftrightarith32bit_1_out_3[24], Out[24], ulacell_8_p7
  // Ulacell ulacell_9: pin names not known; wires that end beside it: shiftrightarith32bit_1_out_3[24], ulacell_8_p7, shiftrightarith32bit_2_out_3[23], ULA_OpCode, shiftrightarith32bit_1_out_3[23], Out[23], ulacell_9_p7
  // Ulacell ulacell_10: pin names not known; wires that end beside it: shiftrightarith32bit_1_out_3[23], ulacell_9_p7, shiftrightarith32bit_2_out_3[22], ULA_OpCode, shiftrightarith32bit_1_out_3[22], Out[22], ulacell_10_p7
  // Ulacell ulacell_11: pin names not known; wires that end beside it: shiftrightarith32bit_1_out_3[22], ulacell_10_p7, shiftrightarith32bit_2_out_3[21], ULA_OpCode, shiftrightarith32bit_1_out_3[21], Out[21], ulacell_11_p7
  // Ulacell ulacell_12: pin names not known; wires that end beside it: shiftrightarith32bit_1_out_3[21], ulacell_11_p7, shiftrightarith32bit_2_out_3[20], ULA_OpCode, shiftrightarith32bit_1_out_3[20], Out[20], ulacell_12_p7
  // Ulacell ulacell_13: pin names not known; wires that end beside it: shiftrightarith32bit_1_out_3[20], ulacell_12_p7, shiftrightarith32bit_2_out_3[19], ULA_OpCode, shiftrightarith32bit_1_out_3[19], Out[19], ulacell_13_p7
  // Ulacell ulacell_14: pin names not known; wires that end beside it: shiftrightarith32bit_1_out_3[18], ulacell_14_p2, shiftrightarith32bit_2_out_3[17], ULA_OpCode, shiftrightarith32bit_1_out_3[17], Out[17], ulacell_14_p7
  // Ulacell ulacell_15: pin names not known; wires that end beside it: shiftrightarith32bit_1_out_3[19], ulacell_13_p7, shiftrightarith32bit_2_out_3[18], ULA_OpCode, shiftrightarith32bit_1_out_3[18], Out[18], ulacell_14_p2
  // Ulacell ulacell_16: pin names not known; wires that end beside it: shiftrightarith32bit_1_out_3[17], ulacell_14_p7, shiftrightarith32bit_2_out_3[16], ULA_OpCode, shiftrightarith32bit_1_out_3[16], Out[16], ulacell_16_p7
  // Ulacell ulacell_17: pin names not known; wires that end beside it: shiftrightarith32bit_1_out_3[15], ulacell_17_p2, shiftrightarith32bit_2_out_3[14], ULA_OpCode, shiftrightarith32bit_1_out_3[14], Out[14], ulacell_17_p7
  // Ulacell ulacell_18: pin names not known; wires that end beside it: shiftrightarith32bit_1_out_3[16], ulacell_16_p7, shiftrightarith32bit_2_out_3[15], ULA_OpCode, shiftrightarith32bit_1_out_3[15], Out[15], ulacell_17_p2
  // Ulacell ulacell_19: pin names not known; wires that end beside it: shiftrightarith32bit_1_out_3[14], ulacell_17_p7, shiftrightarith32bit_2_out_3[13], ULA_OpCode, shiftrightarith32bit_1_out_3[13], Out[13], ulacell_19_p7
  // Ulacell ulacell_20: pin names not known; wires that end beside it: shiftrightarith32bit_1_out_3[12], ulacell_20_p2, shiftrightarith32bit_2_out_3[11], ULA_OpCode, shiftrightarith32bit_1_out_3[11], Out[11], ulacell_20_p7
  // Ulacell ulacell_21: pin names not known; wires that end beside it: shiftrightarith32bit_1_out_3[13], ulacell_19_p7, shiftrightarith32bit_2_out_3[12], ULA_OpCode, shiftrightarith32bit_1_out_3[12], Out[12], ulacell_20_p2
  // Ulacell ulacell_22: pin names not known; wires that end beside it: shiftrightarith32bit_1_out_3[10], ulacell_22_p2, shiftrightarith32bit_2_out_3[9], ULA_OpCode, shiftrightarith32bit_1_out_3[9], Out[9], ulacell_22_p7
  // Ulacell ulacell_23: pin names not known; wires that end beside it: shiftrightarith32bit_1_out_3[11], ulacell_20_p7, shiftrightarith32bit_2_out_3[10], ULA_OpCode, shiftrightarith32bit_1_out_3[10], Out[10], ulacell_22_p2
  // Ulacell ulacell_24: pin names not known; wires that end beside it: shiftrightarith32bit_1_out_3[9], ulacell_22_p7, shiftrightarith32bit_2_out_3[8], ULA_OpCode, shiftrightarith32bit_1_out_3[8], Out[8], ulacell_24_p7
  // Ulacell ulacell_25: pin names not known; wires that end beside it: shiftrightarith32bit_1_out_3[7], ulacell_25_p2, shiftrightarith32bit_2_out_3[6], ULA_OpCode, shiftrightarith32bit_1_out_3[6], Out[6], ulacell_25_p7
  // Ulacell ulacell_26: pin names not known; wires that end beside it: shiftrightarith32bit_1_out_3[8], ulacell_24_p7, shiftrightarith32bit_2_out_3[7], ULA_OpCode, shiftrightarith32bit_1_out_3[7], Out[7], ulacell_25_p2
  // Ulacell ulacell_27: pin names not known; wires that end beside it: shiftrightarith32bit_1_out_3[6], ulacell_25_p7, shiftrightarith32bit_2_out_3[5], ULA_OpCode, shiftrightarith32bit_1_out_3[5], Out[5], ulacell_27_p7
  // Ulacell ulacell_28: pin names not known; wires that end beside it: shiftrightarith32bit_1_out_3[5], ulacell_27_p7, shiftrightarith32bit_2_out_3[4], ULA_OpCode, shiftrightarith32bit_1_out_3[4], Out[4], ulacell_28_p7
  // Ulacell ulacell_29: pin names not known; wires that end beside it: shiftrightarith32bit_1_out_3[4], ulacell_28_p7, shiftrightarith32bit_2_out_3[3], ULA_OpCode, shiftrightarith32bit_1_out_3[3], Out[3], ulacell_29_p7
  // Ulacell ulacell_30: pin names not known; wires that end beside it: shiftrightarith32bit_1_out_3[2], ulacell_30_p2, shiftrightarith32bit_2_out_3[1], ULA_OpCode, shiftrightarith32bit_1_out_3[1], Out[1], ulacell_30_p7
  // Ulacell ulacell_31: pin names not known; wires that end beside it: shiftrightarith32bit_1_out_3[3], ulacell_29_p7, shiftrightarith32bit_2_out_3[2], ULA_OpCode, shiftrightarith32bit_1_out_3[2], Out[2], ulacell_30_p2
  // Ulacell ulacell_32: pin names not known; wires that end beside it: shiftrightarith32bit_1_out_3[1], ulacell_30_p7, shiftrightarith32bit_2_out_3[0], ULA_OpCode, shiftrightarith32bit_1_out_3[0], Out[0], 1'b0

  assign out_4 = Out[0];

  // Notes on the sheet:
  //   00000 - AND
  //   00001 - OR
  //   00010 - SOMADOR
  //   00011 - XOR
  //   00100 - SLL A
  //   00101 - SLL B
  //   00110 - SRL A
  //   00111 - SRL B
  //   01000 - SLA A
  //   01001 - SLA B
  //   01010 - SRA A
  //   01011 - SRA B
  //   01100 - NAND
  //   01101 - NOR
  //   01110 - XNOR
  //   01111 - NOT A
  //   10000 - NOT B
  //   10001 - NOT A+B
  //   10010 - A
  //   10011 - B
endmodule

module projeto (
  input  [31:0] A,
  input  [31:0] B,
  input  [4:0] OP,
  output [31:0] R,
  output out_5
);

  Hex_Digit_Display hex_digit_display_1 (.value(A[31:28]));  // open: dp
  Hex_Digit_Display hex_digit_display_2 (.value(B[31:28]));  // open: dp
  Hex_Digit_Display hex_digit_display_3 (.value(A[23:20]));  // open: dp
  Hex_Digit_Display hex_digit_display_4 (.value(A[27:24]));  // open: dp
  Hex_Digit_Display hex_digit_display_5 (.value(B[27:24]));  // open: dp
  Hex_Digit_Display hex_digit_display_6 (.value(B[23:20]));  // open: dp
  Hex_Digit_Display hex_digit_display_7 (.value(A[15:12]));  // open: dp
  Hex_Digit_Display hex_digit_display_8 (.value(A[19:16]));  // open: dp
  Hex_Digit_Display hex_digit_display_9 (.value(B[15:12]));  // open: dp
  Hex_Digit_Display hex_digit_display_10 (.value(B[19:16]));  // open: dp
  Hex_Digit_Display hex_digit_display_11 (.value(A[11:8]));  // open: dp
  Hex_Digit_Display hex_digit_display_12 (.value(A[7:4]));  // open: dp
  Hex_Digit_Display hex_digit_display_13 (.value(B[11:8]));  // open: dp
  Hex_Digit_Display hex_digit_display_14 (.value(B[7:4]));  // open: dp
  Hex_Digit_Display hex_digit_display_15 (.value(A[3:0]));  // open: dp
  Ulafinal ulafinal_1 (.A(A), .B(B), .out_5(out_5), .Out(R), .ULA_OpCode(OP));  // open: out_4
  Hex_Digit_Display hex_digit_display_16 (.value(B[3:0]));  // open: dp
  Hex_Digit_Display hex_digit_display_17 (.value(R[31:28]));  // open: dp
  Hex_Digit_Display hex_digit_display_18 (.value(R[27:24]));  // open: dp
  Hex_Digit_Display hex_digit_display_19 (.value(R[23:20]));  // open: dp
  Hex_Digit_Display hex_digit_display_20 (.value(R[19:16]));  // open: dp
  Hex_Digit_Display hex_digit_display_21 (.value(R[11:8]));  // open: dp
  Hex_Digit_Display hex_digit_display_22 (.value(R[15:12]));  // open: dp
  Hex_Digit_Display hex_digit_display_23 (.value(R[3:0]));  // open: dp
  Hex_Digit_Display hex_digit_display_24 (.value(R[7:4]));  // open: dp

  // Notes on the sheet:
  //   00000 - AND
  //   00001 - OR
  //   00010 - SOMADOR
  //   00011 - XOR
  //   00100 - SLL A
  //   00101 - SLL B
  //   00110 - SRL A
  //   00111 - SRL B
  //   01000 - SLA A
  //   01001 - SLA B
  //   01010 - SRA A
  //   01011 - SRA B
  //   01100 - NAND
  //   01101 - NOR
  //   01110 - XNOR
  //   01111 - NOT B
  //   10000 - NOT A
  //   10001 - NOT A+B
  //   10010 - B
  //   10011 - A
endmodule
